# Fritzing sketch emisor (saved by Fritzing 0.9.3b)
breadboards: 1

parts:
  Componente2 = NRF24L01+ Breakout Board
  Componente3 = Arduino Uno (Rev3)
  VCC1 = 4 x AAA Battery Mount
  PIR2 = PIR sensor

nets:
  GND: Componente2.GND, Componente3.GND, VCC1.-, PIR2.GND
  N1: Componente2.VCC, VCC1.+
  N2: Componente2.CE, Componente3.D9_PWM
  N3: Componente2.CS, Componente3.D10_PWM/SS
  N4: Componente2.SCK, Componente3.D13/SCK
  N5: Componente2.MOSI, Componente3.D11_PWM/MOSI
  N6: Componente2.MISO, Componente3.D12/MISO
  N7: Componente3.D2, PIR2.SIG
  5V: Componente3.5V, PIR2.VDD
